// Digital circuit tic-tac-toe.dig as structural Verilog
module tic_tac_toe (
);

  wire and_1_out, and_2_out, and_3_out, and_4_out, and_5_out, and_6_out, and_7_out, and_8_out, and_9_out,
       and_10_out, and_11_out, and_12_out, and_13_out, and_14_out, and_15_out, and_16_out, and_17_out,
       and_18_out, and_19_out, and_20_out, and_21_out, and_22_out, and_23_out, and_24_out, and_25_out,
       and_26_out, and_27_out, and_28_out, and_29_out, and_30_out, and_31_out, and_32_out, and_33_out,
       and_34_out, and_35_out, and_36_out, and_37_out, and_38_out, and_39_out, and_40_out, and_41_out,
       and_42_out, and_43_out, and_44_out, draw, End, F1, F2, F3, F4, F5, F6, F7, F8, F9, game_over, O1, O2,
       O3, O4, O5, O6, O7, O8, O9, or_4_out, or_5_out, or_6_out, or_7_out, or_8_out, or_9_out, or_10_out,
       or_11_out, or_12_out, player0, player0_won, player1, player1_won, reset, X1, X2, X3, X4, X5, X6, X7,
       X8, X9;

  and and_1 (and_1_out, F1, ~X1, ~O1);  // And
  and and_2 (and_2_out, F2, ~X2, ~O2);  // And
  and and_3 (and_3_out, F3, ~X3, ~O3);  // And
  and and_4 (and_4_out, F4, ~X4, ~O4);  // And
  and and_5 (and_5_out, F5, ~X5, ~O5);  // And
  and and_6 (and_6_out, F6, ~X6, ~O6);  // And
  and and_7 (and_7_out, F7, ~X7, ~O7);  // And
  and and_8 (and_8_out, F8, ~X8, ~O8);  // And
  and and_9 (and_9_out, F9, ~X9, ~O9);  // And
  or or_1 (End, and_1_out, and_2_out, and_3_out, and_4_out, and_5_out, and_6_out, and_7_out, and_8_out, and_9_out);
  T_FF Player (.T(1'b1), .C(End), .Q(player0), .nQ(player1));
  and and_10 (and_10_out, F1, ~O1, player0, ~game_over);  // And
  and and_11 (and_11_out, F1, ~X1, player1, ~game_over);  // And
  and and_12 (and_12_out, F4, ~O4, player0, ~game_over);  // And
  and and_13 (and_13_out, F4, ~X4, player1, ~game_over);  // And
  and and_14 (and_14_out, F7, ~O7, player0, ~game_over);  // And
  and and_15 (and_15_out, F7, ~X7, player1, ~game_over);  // And
  RS_FF_AS rs_ff_as_1 (.S(and_10_out), .R(reset), .Q(X1));  // open: nQ
  RS_FF_AS rs_ff_as_2 (.S(and_11_out), .R(reset), .Q(O1));  // open: nQ
  RS_FF_AS rs_ff_as_3 (.S(and_12_out), .R(reset), .Q(X4));  // open: nQ
  RS_FF_AS rs_ff_as_4 (.S(and_13_out), .R(reset), .Q(O4));  // open: nQ
  RS_FF_AS rs_ff_as_5 (.S(and_14_out), .R(reset), .Q(X7));  // open: nQ
  RS_FF_AS rs_ff_as_6 (.S(and_15_out), .R(reset), .Q(O7));  // open: nQ
  and and_16 (and_16_out, F2, ~O2, player0, ~game_over);  // And
  and and_17 (and_17_out, F2, ~X2, player1, ~game_over);  // And
  and and_18 (and_18_out, F5, ~O5, player0, ~game_over);  // And
  and and_19 (and_19_out, F5, ~X5, player1, ~game_over);  // And
  and and_20 (and_20_out, F8, ~O8, player0, ~game_over);  // And
  and and_21 (and_21_out, F8, ~X8, player1, ~game_over);  // And
  RS_FF_AS rs_ff_as_7 (.S(and_16_out), .R(reset), .Q(X2));  // open: nQ
  RS_FF_AS rs_ff_as_8 (.S(and_17_out), .R(reset), .Q(O2));  // open: nQ
  RS_FF_AS rs_ff_as_9 (.S(and_18_out), .R(reset), .Q(X5));  // open: nQ
  RS_FF_AS rs_ff_as_10 (.S(and_19_out), .R(reset), .Q(O5));  // open: nQ
  RS_FF_AS rs_ff_as_11 (.S(and_20_out), .R(reset), .Q(X8));  // open: nQ
  RS_FF_AS rs_ff_as_12 (.S(and_21_out), .R(reset), .Q(O8));  // open: nQ
  and and_22 (and_22_out, F3, ~O3, player0, ~game_over);  // And
  and and_23 (and_23_out, F3, ~X3, player1, ~game_over);  // And
  and and_24 (and_24_out, F6, ~O6, player0, ~game_over);  // And
  and and_25 (and_25_out, F6, ~X6, player1, ~game_over);  // And
  and and_26 (and_26_out, F9, ~O9, player0, ~game_over);  // And
  and and_27 (and_27_out, F9, ~X9, player1, ~game_over);  // And
  RS_FF_AS rs_ff_as_13 (.S(and_22_out), .R(reset), .Q(X3));  // open: nQ
  RS_FF_AS rs_ff_as_14 (.S(and_23_out), .R(reset), .Q(O3));  // open: nQ
  RS_FF_AS rs_ff_as_15 (.S(and_24_out), .R(reset), .Q(X6));  // open: nQ
  RS_FF_AS rs_ff_as_16 (.S(and_25_out), .R(reset), .Q(O6));  // open: nQ
  RS_FF_AS rs_ff_as_17 (.S(and_26_out), .R(reset), .Q(X9));  // open: nQ
  RS_FF_AS rs_ff_as_18 (.S(and_27_out), .R(reset), .Q(O9));  // open: nQ
  and and_28 (and_28_out, X1, X2, X3);
  and and_29 (and_29_out, X4, X5, X6);
  and and_30 (and_30_out, X7, X8, X9);
  and and_31 (and_31_out, X1, X4, X7);
  and and_32 (and_32_out, X2, X5, X8);
  and and_33 (and_33_out, X3, X6, X9);
  and and_34 (and_34_out, X1, X5, X9);
  and and_35 (and_35_out, X3, X5, X7);
  or or_2 (player0_won, and_28_out, and_29_out, and_30_out, and_31_out, and_32_out, and_33_out, and_34_out, and_35_out);
  and and_36 (and_36_out, O1, O2, O3);
  and and_37 (and_37_out, O4, O5, O6);
  and and_38 (and_38_out, O7, O8, O9);
  and and_39 (and_39_out, O1, O4, O7);
  and and_40 (and_40_out, O2, O5, O8);
  and and_41 (and_41_out, O3, O6, O9);
  and and_42 (and_42_out, O1, O5, O9);
  and and_43 (and_43_out, O3, O5, O7);
  or or_3 (player1_won, and_36_out, and_37_out, and_38_out, and_39_out, and_40_out, and_41_out, and_42_out, and_43_out);
  or or_4 (or_4_out, X1, O1);
  or or_5 (or_5_out, X2, O2);
  or or_6 (or_6_out, X3, O3);
  or or_7 (or_7_out, X4, O4);
  or or_8 (or_8_out, X5, O5);
  or or_9 (or_9_out, X6, O6);
  or or_10 (or_10_out, X7, O7);
  or or_11 (or_11_out, X8, O8);
  or or_12 (or_12_out, X9, O9);
  and and_44 (and_44_out, or_4_out, or_5_out, or_6_out, or_7_out, or_8_out, or_9_out, or_10_out, or_11_out, or_12_out);
  and and_45 (draw, and_44_out, ~player0_won, ~player1_won);  // And
  LED led_1 (.in(X1));
  LED led_2 (.in(O1));
  LED led_3 (.in(X4));
  LED led_4 (.in(O4));
  LED led_5 (.in(X7));
  LED led_6 (.in(O7));
  Button button_1 (.out(F1));
  Button button_2 (.out(F4));
  Button button_3 (.out(F7));
  Button button_4 (.out(F2));
  Button button_5 (.out(F5));
  Button button_6 (.out(F8));
  LED led_7 (.in(X2));
  LED led_8 (.in(O2));
  LED led_9 (.in(X5));
  LED led_10 (.in(O5));
  LED led_11 (.in(X8));
  LED led_12 (.in(O8));
  Button button_7 (.out(F3));
  Button button_8 (.out(F6));
  Button button_9 (.out(F9));
  Button button_10 (.out(reset));
  LED led_13 (.in(X3));
  LED led_14 (.in(O3));
  LED led_15 (.in(X6));
  LED led_16 (.in(O6));
  LED led_17 (.in(X9));
  LED led_18 (.in(O9));
  LED led_19 (.in(player0_won));
  LED led_20 (.in(player1_won));
  LED led_21 (.in(draw));
  or or_13 (game_over, player0_won, player1_won, draw);

  // Notes on the sheet:
  //   Toggles the player by end of turn.
  //   0: Player X
  //   1: Player O
  //   The game state is stored in these Flip-Flops. Each cell of the
  //   field is represented by a 2 bit value:
  //   00: Empty
  //   01: X
  //   10: O
  //   This logic decides whether player 0 (X) has won.
  //   This logic decides whether player 1 (O) has won.
  //   This logic detects draws.
  //   This is the visual representation of the tic tac toe game.
  //   Red: X
  //   Blue: O
endmodule
